// Logisim project alu.circ as structural Verilog: 2 circuits, main circuit y01d
module y01d (
  input  in_1,
  input  [7:0] in_2,
  input  [7:0] in_3,
  input  [1:0] sel,
  output [7:0] out_5,
  output out_6
);

  wire adder_1_cout, subtractor_1_bout;
  wire [7:0] adder_1_out, demultiplexer_1_out0, demultiplexer_1_out1, demultiplexer_1_out3,
       demultiplexer_2_out0, demultiplexer_2_out1, demultiplexer_2_out2, demultiplexer_2_out3, nor_1_out,
       subtractor_1_out, xor_1_out;

  Demultiplexer #(.select(2), .width(8)) demultiplexer_1 (
    .out0(demultiplexer_1_out0), .out1(demultiplexer_1_out1), .out2(demultiplexer_1_out1),
    .out3(demultiplexer_1_out3), .in(in_2), .sel(sel));  // open: en
  Demultiplexer #(.select(2), .width(8)) demultiplexer_2 (
    .out0(demultiplexer_2_out0), .out1(demultiplexer_2_out1), .out2(demultiplexer_2_out2),
    .out3(demultiplexer_2_out3), .in(in_3), .sel(sel));  // open: en
  Adder adder_1 (
    .a(demultiplexer_1_out0), .b(demultiplexer_2_out0), .out(adder_1_out), .cin(in_1), .cout(adder_1_cout));
  Subtractor subtractor_1 (
    .a(demultiplexer_1_out1), .b(demultiplexer_2_out1), .out(subtractor_1_out), .bin(in_1),
    .bout(subtractor_1_bout));
  assign xor_1_out = demultiplexer_1_out1 ^ demultiplexer_2_out2;  // XOR_Gate xor_1, 8 bits wide
  assign nor_1_out = ~(demultiplexer_1_out3 | demultiplexer_2_out3);  // NOR_Gate nor_1, 8 bits wide
  Multiplexer #(.select(2), .width(8)) multiplexer_1 (
    .in0(adder_1_out), .in1(subtractor_1_out), .in2(xor_1_out), .in3(nor_1_out), .out(out_5), .sel(sel));  // open: en
  Multiplexer #(.select(2)) multiplexer_2 (
    .in0(adder_1_cout), .in1(subtractor_1_bout), .out(out_6), .sel(sel));  // open: in2, in3, en
endmodule

module ALU (
  input  in_1,
  input  [7:0] in_2,
  input  [7:0] in_3,
  input  [1:0] in_4
);

  wire y01d_1_out_6;
  wire [7:0] y01d_1_out_5;

  y01d y01d_1 (.in_2(in_2), .in_3(in_3), .in_1(in_1), .sel(in_4), .out_5(y01d_1_out_5), .out_6(y01d_1_out_6));
  Hex_Digit_Display hex_digit_display_1 (.value(y01d_1_out_5[3:0]));  // open: dp
  Hex_Digit_Display hex_digit_display_2 (.value(y01d_1_out_5[7:4]));  // open: dp
endmodule
