// Logisim project aufg11_1.circ as structural Verilog: 4 circuits, main circuit y01d
module y01d (
  input  Optionaler_Carry_In,
  input  [2:0] opcode,
  input  [1:0] Z_REG,
  input  [1:0] X_REG,
  input  [1:0] Y_REG,
  input  [7:0] immediate,
  output out_7
);

  wire clock_out;
  wire [7:0] multiplexer_1_out, multiplexer_2_out, n8_bit_alu_rechenwerk_1_out,
       register_speicherwerk_1_out_x, register_speicherwerk_1_out_y;

  Clock clock (.out(clock_out));
  Multiplexer #(.select(3), .width(8)) multiplexer_1 (
    .in0(n8_bit_alu_rechenwerk_1_out), .in1(n8_bit_alu_rechenwerk_1_out), .in2(n8_bit_alu_rechenwerk_1_out),
    .in3({8{1'b0}}), .in4(n8_bit_alu_rechenwerk_1_out), .in5(n8_bit_alu_rechenwerk_1_out),
    .in6(n8_bit_alu_rechenwerk_1_out), .in7(n8_bit_alu_rechenwerk_1_out), .out(multiplexer_1_out),
    .sel(opcode));  // open: en
  Register___Speicherwerk register_speicherwerk_1 (
    .clock(clock_out), .\input (multiplexer_1_out), .out_y(register_speicherwerk_1_out_y),
    .out_x(register_speicherwerk_1_out_x), .R___W(2'b11), .sel_z(Z_REG), .sel_x(X_REG), .sel_y(Y_REG));
  Multiplexer #(.select(3), .width(8)) multiplexer_2 (
    .in0(register_speicherwerk_1_out_y), .in1(register_speicherwerk_1_out_y),
    .in2(register_speicherwerk_1_out_y), .in4(register_speicherwerk_1_out_y),
    .in5(register_speicherwerk_1_out_y), .in6(immediate), .in7(immediate), .out(multiplexer_2_out),
    .sel(opcode));  // open: in3, en
  _8_Bit_ALU___Rechenwerk u_8_bit_alu_rechenwerk_1 (
    .In_X(register_speicherwerk_1_out_x), .In_Y(multiplexer_2_out), .out(n8_bit_alu_rechenwerk_1_out),
    .overflow___carry_out(out_7), .Carry_In(Optionaler_Carry_In), .S1(opcode));
  Hex_Digit_Display hex_digit_display_1 (.value(register_speicherwerk_1_out_y[3:0]));  // open: dp
  Hex_Digit_Display hex_digit_display_2 (.value(register_speicherwerk_1_out_y[7:4]));  // open: dp
  Hex_Digit_Display hex_digit_display_3 (.value(register_speicherwerk_1_out_x[7:4]));  // open: dp
  Hex_Digit_Display hex_digit_display_4 (.value(register_speicherwerk_1_out_x[3:0]));  // open: dp

  // Notes on the sheet:
  //   Beispiel:
  //   Rechenwerk <->
  //   CPU & GPU
  //   addi $3, $3, 5 => 110 11 11 00000101
  //   addi $2, $2, 10 => 110 10 10 00001010
  //   add $0, $3, $2 = > 100 11 10
  //   (Was im immediate steht ist bei allem außer addi & subi egal)
  //   Eingabewerk
  //   z.B. Maus & Tastatur
  //   |
  //   V
  //   Steuerwerk
  //   |
  //   V
  //   Ausgabewerk
  //   Monitor, Lautsprecher, usw
  //   => Register $3 += 5
  //   => Register $2 += 10
  //   => Register $0 = F
  //    <-> Speicherwerk
  //   Eingabewerk ^
  //   RAM & Speicher (SSD / HDD)
  //   Hier wird das Ergebnis 
  //   in Register Z gespeichert ->
  //   Gibt im Fall von 011 (Reset Register)
  //   0x00 als input zum Speichern an ->
  //   nach Tawdross's Angaben
  //   Überprüft die
  //   beiden Im-
  //   mediate Fälle
  //   |->
  //   (110 und 111)
  //   Von-Neumann-Rechner
  //   <- Führt den Command der im Eingabewerk steht aus
  //   <- Muss immer auf 11 (3 dec) sein
  //   Steuerwerk
  //   Steuerwerk + Rechenwerk = CPU
  //   <- mit x wird immer
  //   gerechnet, egal ob
  //   immediate oder 
  //   register opcode
  //   Steuerwerk
  //   Die beiden MUX'e und alle Kabel (Steuerbusse) bilden das Steuerwerk
  //   y ->
  //   8* 1-bit-ALU's
  //   Ausgabewerk
  //   -> 8 bit Rechenwerk
  //   <- x
endmodule

module Register___Speicherwerk (
  input  clock,
  input  [1:0] R___W,
  input  [7:0] \input ,
  input  [1:0] sel_z,
  input  [1:0] sel_x,
  input  [1:0] sel_y,
  output [7:0] out_y,
  output [7:0] out_x
);

  wire and_1_out, demultiplexer_1_out0, demultiplexer_1_out1, demultiplexer_1_out2, demultiplexer_1_out3;
  wire [1:0] demultiplexer_2_out1, demultiplexer_2_out3, demultiplexer_3_out2, demultiplexer_3_out3,
       demultiplexer_4_out2, demultiplexer_4_out3, or_1_out, or_2_out, or_3_out;
  wire [7:0] register_1_q, register_2_q, register_3_q, register_4_q;

  and and_1 (and_1_out, demultiplexer_1_out0, R___W[0]);
  Demultiplexer #(.select(2)) demultiplexer_1 (
    .out0(demultiplexer_1_out0), .out1(demultiplexer_1_out1), .out2(demultiplexer_1_out2),
    .out3(demultiplexer_1_out3), .in(clock), .sel(or_1_out));  // open: en
  Register register_1 (.D(\input ), .Q(register_1_q), .clk(and_1_out));  // open: en, clr
  Register register_2 (.D(\input ), .Q(register_2_q), .clk(demultiplexer_1_out2));  // open: en, clr
  Register register_3 (.D(\input ), .Q(register_3_q), .clk(demultiplexer_1_out1));  // open: en, clr
  Register register_4 (.D(\input ), .Q(register_4_q), .clk(demultiplexer_1_out3));  // open: en, clr
  assign or_1_out = demultiplexer_2_out1 | demultiplexer_2_out3;  // OR_Gate or_1, 2 bits wide
  Demultiplexer #(.select(2), .width(2)) demultiplexer_2 (
    .out1(demultiplexer_2_out1), .out3(demultiplexer_2_out3), .in(sel_z), .sel(R___W));  // open: out0, out2, en
  assign or_2_out = demultiplexer_3_out2 | demultiplexer_3_out3;  // OR_Gate or_2, 2 bits wide
  Demultiplexer #(.select(2), .width(2)) demultiplexer_3 (
    .out2(demultiplexer_3_out2), .out3(demultiplexer_3_out3), .in(sel_x), .sel(R___W));  // open: out0, out1, en
  assign or_3_out = demultiplexer_4_out2 | demultiplexer_4_out3;  // OR_Gate or_3, 2 bits wide
  Demultiplexer #(.select(2), .width(2)) demultiplexer_4 (
    .out2(demultiplexer_4_out2), .out3(demultiplexer_4_out3), .in(sel_y), .sel(R___W));  // open: out0, out1, en
  Multiplexer #(.select(2), .width(8)) multiplexer_1 (
    .in0(register_1_q), .in1(register_3_q), .in2(register_2_q), .in3(register_4_q), .out(out_y),
    .sel(or_3_out));  // open: en
  Multiplexer #(.select(2), .width(8)) multiplexer_2 (
    .in0(register_1_q), .in1(register_3_q), .in2(register_2_q), .in3(register_4_q), .out(out_x),
    .sel(or_2_out));  // open: en

  // Notes on the sheet:
  //   Das heisst der enable Eingang kann
  //   komplett ignoriert werden
  //   Der input ist immer an Alle register angeschlossen,
  //   die Werte werden aber nur überschrieben, wenn die
  //   clock auch durchgeht                                           ->
  //   Bugfix, damit die clock nur bei 01 oder 11 durchgeht ->
  //   output vom Rechenwerk kommt hier rein 
  //   Bei dieser aufgabe kann R / W ignoriert werden,
  //   da bei diesem Rechner immer geschrieben und
  //   gelesen werden muss, sodass R/W immer auf 11 ist
  //   Speicherwerk
  //   Kann 1 Register von 4 Beschreiben, und 2 Register gleichzeitig ausgeben
  //   z ist nur für den input
  //   <- Die OR-Gatter sorgen dafür, dass
  //   in beiden Fällen, also Read und 
  //   Read & Write (gleichzeitig)
  //   der output ausgegeben wird.
  //   Read = 10
  //   Write = 01
  //   Read & Write = 11
  //   <- x & y sind nur für die outputs
endmodule

module _8_Bit_ALU___Rechenwerk (
  input  Carry_In,
  input  [7:0] In_X,
  input  [7:0] In_Y,
  input  [2:0] S1,
  output [7:0] out,
  output overflow___carry_out
);

  wire alu_1_carry_out, alu_2_carry_out, alu_3_carry_out, alu_4_carry_out, alu_5_carry_out, alu_6_carry_out,
       alu_7_carry_out;

  ALU alu_1 (.X(In_X[0]), .Y(In_Y[0]), .out(out[0]), .carry_out(alu_1_carry_out), .carry_in(Carry_In), .M_S1_S2(S1));
  ALU alu_2 (
    .X(In_X[4]), .Y(In_Y[4]), .out(out[4]), .carry_out(alu_2_carry_out), .carry_in(alu_7_carry_out),
    .M_S1_S2(S1));
  ALU alu_3 (
    .X(In_X[1]), .Y(In_Y[1]), .out(out[1]), .carry_out(alu_3_carry_out), .carry_in(alu_1_carry_out),
    .M_S1_S2(S1));
  ALU alu_4 (
    .X(In_X[5]), .Y(In_Y[5]), .out(out[5]), .carry_out(alu_4_carry_out), .carry_in(alu_2_carry_out),
    .M_S1_S2(S1));
  ALU alu_5 (
    .X(In_X[2]), .Y(In_Y[2]), .out(out[2]), .carry_out(alu_5_carry_out), .carry_in(alu_3_carry_out),
    .M_S1_S2(S1));
  ALU alu_6 (
    .X(In_X[6]), .Y(In_Y[6]), .out(out[6]), .carry_out(alu_6_carry_out), .carry_in(alu_4_carry_out),
    .M_S1_S2(S1));
  ALU alu_7 (
    .X(In_X[3]), .Y(In_Y[3]), .out(out[3]), .carry_out(alu_7_carry_out), .carry_in(alu_5_carry_out),
    .M_S1_S2(S1));
  ALU alu_8 (
    .X(In_X[7]), .Y(In_Y[7]), .out(out[7]), .carry_out(overflow___carry_out), .carry_in(alu_6_carry_out),
    .M_S1_S2(S1));

  // Notes on the sheet:
  //   Kleinstes Bit ->
  //   x ->
  //   y - >
  //   opcode
  //   out
  //   carry out
  //   Rechenwerk
  //   verbindet die 1-bit-ALU's zu einer 8-bit-ALU
  //   <- größtes Bit
endmodule

module ALU (
  input  carry_in,
  input  X,
  input  Y,
  input  [2:0] M_S1_S2,
  output out,
  output carry_out
);

  wire adder_1_cout, adder_1_out, adder_2_cout, adder_2_out, NAND_out, nor_1_out, subtractor_1_bout,
       subtractor_1_out, subtractor_2_bout, subtractor_2_out, XOR_out;
  wire [1:0] demultiplexer_1_out0, demultiplexer_1_out1, demultiplexer_1_out2, demultiplexer_1_out4,
       demultiplexer_1_out5, demultiplexer_1_out6, demultiplexer_1_out7;

  Demultiplexer #(.select(3), .width(2)) demultiplexer_1 (
    .out0(demultiplexer_1_out0), .out1(demultiplexer_1_out1), .out2(demultiplexer_1_out2),
    .out4(demultiplexer_1_out4), .out5(demultiplexer_1_out5), .out6(demultiplexer_1_out6),
    .out7(demultiplexer_1_out7), .in({Y, X}), .sel(M_S1_S2));  // open: out3, en
  nor nor_1 (nor_1_out, demultiplexer_1_out0[0], demultiplexer_1_out0[1]);
  nand NAND (NAND_out, demultiplexer_1_out1[0], demultiplexer_1_out1[1]);
  xor XOR (XOR_out, demultiplexer_1_out2[0], demultiplexer_1_out2[1]);
  Adder #(.width(1)) adder_1 (
    .a(demultiplexer_1_out4[0]), .b(demultiplexer_1_out4[1]), .out(adder_1_out), .cin(carry_in),
    .cout(adder_1_cout));
  Subtractor #(.width(1)) subtractor_1 (
    .a(demultiplexer_1_out5[0]), .b(demultiplexer_1_out5[1]), .out(subtractor_1_out), .bin(carry_in),
    .bout(subtractor_1_bout));
  Adder #(.width(1)) adder_2 (
    .a(demultiplexer_1_out6[0]), .b(demultiplexer_1_out6[1]), .out(adder_2_out), .cin(carry_in),
    .cout(adder_2_cout));
  Subtractor #(.width(1)) subtractor_2 (
    .a(demultiplexer_1_out7[0]), .b(demultiplexer_1_out7[1]), .out(subtractor_2_out), .bin(carry_in),
    .bout(subtractor_2_bout));
  Multiplexer #(.select(3)) multiplexer_1 (
    .in0(nor_1_out), .in1(NAND_out), .in2(XOR_out), .in4(adder_1_out), .in5(subtractor_1_out),
    .in6(adder_2_out), .in7(subtractor_2_out), .out(out), .sel(M_S1_S2));  // open: in3, en
  Multiplexer #(.select(3)) multiplexer_2 (
    .in4(adder_1_cout), .in5(subtractor_1_bout), .in6(adder_2_cout), .in7(subtractor_2_bout),
    .out(carry_out), .sel(M_S1_S2));  // open: in0, in1, in2, in3, en

  // Notes on the sheet:
  //   opcode ->
  //   Die oberen + und - sind
  //   exakt gleich zu den unteren,
  //   man braucht aber trotzdem
  //   beide, da die unteren Fälle für opcodes 110 und 111 sind
  //   NOR
  //   add
  //   sub
  //   addi
  //   subi
  //   1-Bit-ALU
endmodule
