// Logisim project aufg2_1.circ as structural Verilog: 1 circuit, main circuit y01d
module y01d (
  input  _3,
  input  _2,
  input  _1,
  input  _0,
  input  in_5,
  input  in_6,
  input  in_7,
  input  in_8,
  output y0,
  output y1,
  output y2,
  output y3
);

  ROM #(.addrWidth(4), .dataWidth(1)) rom_1 (.addr({_3, _2, _1, _0}), .data(y0), .sel(in_5));
  ROM #(.addrWidth(4), .dataWidth(1)) rom_2 (.addr({_3, _2, _1, _0}), .data(y1), .sel(in_6));
  ROM #(.addrWidth(4), .dataWidth(1)) rom_3 (.addr({_3, _2, _1, _0}), .data(y2), .sel(in_7));
  ROM #(.addrWidth(4), .dataWidth(1)) rom_4 (.addr({_3, _2, _1, _0}), .data(y3), .sel(in_8));

  // Notes on the sheet:
  //   contents of rom_1 (hex, n*v repeats v):
  //   5*0 1 0 1 5*0 1 0 1
  //   contents of rom_2 (hex, n*v repeats v):
  //   5*0 1 1 1 0 1 1 1 0 1 1
  //   contents of rom_3 (hex, n*v repeats v):
  //   10*0 1 1 0 0 1
  //   contents of rom_4 (hex, n*v repeats v):
  //   15*0 1
endmodule
