// Logisim project aufg2_2.circ as structural Verilog: 1 circuit, main circuit y01d
module y01d (
  input  _3,
  input  _2,
  input  _1,
  input  _0,
  input  in_5,
  output y
);

  ROM #(.addrWidth(4), .dataWidth(1)) rom_1 (.addr({_3, _2, _1, _0}), .data(y), .sel(in_5));

  // Notes on the sheet:
  //   2)
  //   a) 1 zu 0, kann nicht glitchen
  //   b) 0 zu 0, kann zur 1 glitchen
  //   c)  1 zu 0, kann nicht glitchen
  //   d)  kein hazard, 0000 = 0001 = 0100 = 0101
  //   e) kein hazrad, von 0101 zu 1101
  //   contents of rom_1 (hex, n*v repeats v):
  //   1 1 0 0 1 1 0 0 0 1 0 1 0 1 0 1
endmodule
