// Logisim project aufg4_1d.circ as structural Verilog: 1 circuit, main circuit y01d
module y01d (
);

  wire and_1_out, and_2_out, and_3_out, and_4_out, and_5_out, and_6_out, and_7_out, and_8_out, and_9_out,
       and_10_out, and_11_out, and_12_out, and_13_out, and_14_out, and_15_out, d_ff_1_qn, d_ff_2_qn,
       d_ff_3_qn, not_1_out, not_2_out, not_3_out, or_1_out, or_2_out, or_3_out, or_4_out, or_5_out;
  wire [1:0] rom_2_data;
  wire [3:0] clock_1_out;
  wire [4:0] rom_1_data;

  Clock clock_1 (.out(clock_1_out[0]));
  D_Flip_Flop d_ff_1 (
    .clk(clock_1_out[0]), .D(d_ff_1_qn), .Q(clock_1_out[1]), .Qn(d_ff_1_qn));  // open: preset, en, reset
  not not_1 (not_1_out, d_ff_2_qn);
  not not_2 (not_2_out, d_ff_1_qn);
  and and_1 (and_1_out, not_1_out, not_2_out);
  and and_2 (and_2_out, ~not_3_out, not_1_out, ~not_2_out);  // AND_Gate
  and and_3 (and_3_out, not_3_out, not_2_out);
  and and_4 (and_4_out, not_1_out, ~not_2_out, ~clock_1_out[0]);  // AND_Gate
  and and_5 (and_5_out, ~not_1_out, ~not_2_out, clock_1_out[0]);  // AND_Gate
  and and_6 (and_6_out, ~not_3_out, not_2_out, clock_1_out[0]);  // AND_Gate
  and and_7 (and_7_out, not_2_out, clock_1_out[0]);
  and and_8 (and_8_out, ~not_3_out, ~not_1_out, not_2_out);  // AND_Gate
  and and_9 (and_9_out, not_3_out, ~not_1_out, ~not_2_out, ~clock_1_out[0]);  // AND_Gate
  and and_10 (and_10_out, ~not_3_out, not_1_out, ~not_2_out, ~clock_1_out[0]);  // AND_Gate
  and and_11 (and_11_out, not_3_out, not_1_out);
  and and_12 (and_12_out, not_3_out, ~not_2_out);  // AND_Gate
  and and_13 (and_13_out, not_1_out, ~not_2_out, clock_1_out[0]);  // AND_Gate
  and and_14 (and_14_out, not_3_out, ~not_1_out, ~not_2_out, clock_1_out[0]);  // AND_Gate
  and and_15 (and_15_out, not_3_out, ~not_1_out, not_2_out, clock_1_out[0]);  // AND_Gate
  D_Flip_Flop d_ff_2 (
    .clk(clock_1_out[1]), .D(d_ff_2_qn), .Q(clock_1_out[2]), .Qn(d_ff_2_qn));  // open: preset, en, reset
  not not_3 (not_3_out, d_ff_3_qn);
  D_Flip_Flop d_ff_3 (
    .clk(clock_1_out[2]), .D(d_ff_3_qn), .Q(clock_1_out[3]), .Qn(d_ff_3_qn));  // open: preset, en, reset
  or or_1 (or_1_out, not_3_out, and_1_out);
  or or_2 (or_2_out, and_2_out, and_3_out);
  or or_3 (or_3_out, and_4_out, and_5_out, and_6_out);
  or or_4 (or_4_out, and_7_out, and_8_out, and_9_out, and_10_out);
  or or_5 (or_5_out, and_11_out, and_12_out, and_13_out);
  ROM #(.addrWidth(4), .dataWidth(5)) rom_1 (.addr(clock_1_out), .data(rom_1_data), .sel(1'b1));
  ROM #(.addrWidth(4), .dataWidth(2)) rom_2 (.addr(clock_1_out), .data(rom_2_data), .sel(1'b1));

  // Notes on the sheet:
  //   4.1
  //   0     1    2     3 
  //   b) Es werden 3 Zustandsvariabeln benötigt, da man 7 Zustände hat
  //   4.2 e)
  //   a) Es handelt sich um ein Moore FSM, da die Outputs in den Zuständen stehen
  //   4.2
  //   a) Es werden 4 Zustandsvariablen benötigt, und die validen Zustände sind die Zahlen 1 bis 2^4 in binär
  //   contents of rom_1 (hex, n*v repeats v):
  //   0 4 8 c e 12 1 d 19 15 3 b 15 11
  //   4.2 c)
  //   contents of rom_2 (hex, n*v repeats v):
  //   9*0 2 0 1
endmodule
