// Logisim project aufg4_1new.circ as structural Verilog: 1 circuit, main circuit main
module main (
  input  in_1,
  output out_2,
  output out_3
);

  wire and_1_out, and_2_out, and_3_out, and_4_out, and_5_out, and_6_out, and_7_out, and_8_out, and_9_out,
       and_10_out, and_11_out, and_12_out, and_13_out, clock_1_out, d_ff_4_q, d_ff_5_q, d_ff_6_q, or_1_out,
       or_2_out, or_3_out, or_4_out, or_5_out;
  wire [3:1] d_ff_1_q;
  wire [4:2] rom_1_data;

  Clock clock_1 (.out(clock_1_out));
  D_Flip_Flop d_ff_1 (.clk(clock_1_out), .D(rom_1_data[2]), .Q(d_ff_1_q[1]));  // open: Qn, preset, en, reset
  D_Flip_Flop d_ff_2 (.clk(clock_1_out), .D(rom_1_data[3]), .Q(d_ff_1_q[2]));  // open: Qn, preset, en, reset
  D_Flip_Flop d_ff_3 (.clk(clock_1_out), .D(rom_1_data[4]), .Q(d_ff_1_q[3]));  // open: Qn, preset, en, reset
  D_Flip_Flop d_ff_4 (.clk(clock_1_out), .D(or_3_out), .Q(d_ff_4_q));  // open: Qn, preset, en, reset
  D_Flip_Flop d_ff_5 (.clk(clock_1_out), .D(or_4_out), .Q(d_ff_5_q));  // open: Qn, preset, en, reset
  D_Flip_Flop d_ff_6 (.clk(clock_1_out), .D(or_5_out), .Q(d_ff_6_q));  // open: Qn, preset, en, reset
  ROM #(.addrWidth(4), .dataWidth(5)) rom_1 (.addr({d_ff_1_q, in_1}), .data({rom_1_data, out_2, out_3}));  // open: sel
  and and_1 (and_1_out, d_ff_5_q, d_ff_4_q);
  and and_2 (and_2_out, ~d_ff_6_q, d_ff_5_q, ~d_ff_4_q);  // AND_Gate
  and and_3 (and_3_out, d_ff_6_q, d_ff_4_q);
  and and_4 (and_4_out, d_ff_5_q, ~d_ff_4_q, ~in_1);  // AND_Gate
  and and_5 (and_5_out, ~d_ff_5_q, ~d_ff_4_q, in_1);  // AND_Gate
  and and_6 (and_6_out, ~d_ff_6_q, d_ff_4_q, in_1);  // AND_Gate
  and and_7 (and_7_out, d_ff_4_q, in_1);
  and and_8 (and_8_out, ~d_ff_6_q, ~d_ff_5_q, d_ff_4_q);  // AND_Gate
  and and_9 (and_9_out, d_ff_6_q, ~d_ff_5_q, ~d_ff_4_q, ~in_1);  // AND_Gate
  and and_10 (and_10_out, ~d_ff_6_q, d_ff_5_q, ~d_ff_4_q, ~in_1);  // AND_Gate
  and and_11 (and_11_out, d_ff_6_q, d_ff_5_q);
  and and_12 (and_12_out, d_ff_6_q, ~d_ff_4_q);  // AND_Gate
  and and_13 (and_13_out, d_ff_5_q, ~d_ff_4_q, in_1);  // AND_Gate
  or or_1 (or_1_out, d_ff_6_q, and_1_out);
  or or_2 (or_2_out, and_2_out, and_3_out);
  or or_3 (or_3_out, and_4_out, and_5_out, and_6_out);
  or or_4 (or_4_out, and_7_out, and_8_out, and_9_out, and_10_out);
  or or_5 (or_5_out, and_11_out, and_12_out, and_13_out);

  // Notes on the sheet:
  //   contents of rom_1 (hex, n*v repeats v):
  //   0 4 8 c e 12 1 d 19 15 3 b 15 11
endmodule
