// Logisim project aufg8_1.circ as structural Verilog: 1 circuit, main circuit y01d
module y01d (
  input  _3,
  input  _2,
  input  _1,
  input  _0,
  input  debug,
  output out_6
);

  Multiplexer #(.select(4)) multiplexer_1 (
    .in0(debug), .in1(1'b1), .in2(debug), .in3(debug), .in4(1'b1), .in5(debug), .in6(1'b1), .in7(1'b1),
    .in8(debug), .in9(1'b1), .in10(1'b1), .in11(debug), .in12(1'b1), .in13(1'b1), .in14(debug), .in15(debug),
    .out(out_6), .sel({_3, _2, _1, _0}));  // open: en
endmodule
