// Logisim project aufg8_2.circ as structural Verilog: 2 circuits, main circuit y01d
module y01d (
  input  R___W,
  input  [7:0] in_2,
  input  [1:0] select,
  output [7:0] out
);

  wire clock_1_out;

  Clock clock_1 (.out(clock_1_out));
  Circut2 circut2_1 (._8___Bit_in(in_2), .clock(R___W), .R___W(clock_1_out), .select(select), .out(out));
endmodule

module Circut2 (
  input  clock,
  input  R___W,
  input  [1:0] select,
  input  [7:0] _8___Bit_in,
  output [7:0] out
);

  wire and_1_out, demultiplexer_1_out0, demultiplexer_1_out1, demultiplexer_1_out2, demultiplexer_1_out3;
  wire [1:0] demultiplexer_2_out0, demultiplexer_2_out1;
  wire [7:0] register_1_q, register_2_q, register_3_q, register_4_q;

  Demultiplexer #(.select(2)) demultiplexer_1 (
    .out0(demultiplexer_1_out0), .out1(demultiplexer_1_out1), .out2(demultiplexer_1_out2),
    .out3(demultiplexer_1_out3), .in(clock), .sel(demultiplexer_2_out1));  // open: en
  and and_1 (and_1_out, demultiplexer_1_out0, R___W);
  Register register_1 (.D(_8___Bit_in), .Q(register_1_q), .clk(and_1_out));  // open: en, clr
  Register register_2 (.D(_8___Bit_in), .Q(register_2_q), .clk(demultiplexer_1_out1));  // open: en, clr
  Register register_3 (.D(_8___Bit_in), .Q(register_3_q), .clk(demultiplexer_1_out2));  // open: en, clr
  Register register_4 (.D(_8___Bit_in), .Q(register_4_q), .clk(demultiplexer_1_out3));  // open: en, clr
  Demultiplexer #(.width(2)) demultiplexer_2 (
    .out0(demultiplexer_2_out0), .out1(demultiplexer_2_out1), .in(select), .sel(R___W));  // open: en
  Multiplexer #(.select(2), .width(8)) multiplexer_1 (
    .in0(register_1_q), .in1(register_2_q), .in2(register_3_q), .in3(register_4_q), .out(out),
    .sel(demultiplexer_2_out0));  // open: en
endmodule
