// Logisim project aufg9_1.circ as structural Verilog: 5 circuits, main circuit y01d
module y01d (
  input  [7:0] test_x,
  input  [7:0] test_y,
  input  carry_in,
  input  [2:0] S,
  input  [31:0] test_x_2,
  input  [31:0] test_y_2,
  input  carry_in_2,
  input  [2:0] S_2
);

  wire n8_bit_alu_2_1_overflow___carry_out, n32_bit_alu_1_overflow___carry_out;
  wire [3:0] n32_bit_alu_1_out_2;
  wire [7:0] n8_bit_alu_2_1_out;
  wire [31:0] n32_bit_alu_1_out;

  _32_Bit_ALU u_32_bit_alu_1 (
    .In_X(test_x_2), .In_Y(test_y_2),
    .out({n32_bit_alu_1_out[31:8], n32_bit_alu_1_out_2, n32_bit_alu_1_out[3:0]}),
    .overflow___carry_out(n32_bit_alu_1_overflow___carry_out), .Carry_In(carry_in_2), .S1(S_2));
  _8_Bit_alu_2 u_8_bit_alu_2_1 (
    .In_X(test_x), .In_Y(test_y), .out(n8_bit_alu_2_1_out),
    .overflow___carry_out(n8_bit_alu_2_1_overflow___carry_out), .Carry_In(carry_in), .S1(S));
  // Probe on n32_bit_alu_1_overflow___carry_out
  // Probe on n8_bit_alu_2_1_overflow___carry_out
  Hex_Digit_Display hex_digit_display_1 (.value(n8_bit_alu_2_1_out[3:0]));  // open: dp
  Hex_Digit_Display hex_digit_display_2 (.value(n8_bit_alu_2_1_out[7:4]));  // open: dp
  Hex_Digit_Display hex_digit_display_3 (.value(n32_bit_alu_1_out[27:24]));  // open: dp
  Hex_Digit_Display hex_digit_display_4 (.value(n32_bit_alu_1_out[31:28]));  // open: dp
  Hex_Digit_Display hex_digit_display_5 (.value(n32_bit_alu_1_out[23:20]));  // open: dp
  Hex_Digit_Display hex_digit_display_6 (.value(n32_bit_alu_1_out[19:16]));  // open: dp
  TTY tty_1 (.data(n8_bit_alu_2_1_out[6:0]), .clk(carry_in));  // open: we, clr
  Hex_Digit_Display hex_digit_display_7 (.value(n32_bit_alu_1_out[15:12]));  // open: dp
  Hex_Digit_Display hex_digit_display_8 (.value(n32_bit_alu_1_out_2));  // open: dp
  Hex_Digit_Display hex_digit_display_9 (.value(n32_bit_alu_1_out[11:8]));  // open: dp
  Hex_Digit_Display hex_digit_display_10 (.value(n32_bit_alu_1_out[3:0]));  // open: dp
endmodule

module _8_Bit_ALU (
  input  [7:0] In_X,
  input  [7:0] In_Y,
  input  M,
  input  S1,
  input  S2,
  output [7:0] out,
  output overflow
);

  wire alu_1_p7, alu_2_p4, alu_2_p8, alu_3_p8, alu_4_p8, alu_5_p8, alu_6_p8;

  // ALU alu_1: pin names not known; wires that end beside it: In_X[0], In_Y[0], M, S1, S2, out[0], alu_1_p7
  // ALU alu_2: pin names not known; wires that end beside it: In_X[4], In_Y[4], M, alu_2_p4, S1, S2, out[4], alu_2_p8
  // ALU alu_3: pin names not known; wires that end beside it: In_X[1], In_Y[1], M, alu_1_p7, S1, S2, out[1], alu_3_p8
  // ALU alu_4: pin names not known; wires that end beside it: In_X[5], In_Y[5], M, alu_2_p8, S1, S2, out[5], alu_4_p8
  // ALU alu_5: pin names not known; wires that end beside it: In_X[2], In_Y[2], M, alu_3_p8, S1, S2, out[2], alu_5_p8
  // ALU alu_6: pin names not known; wires that end beside it: In_X[6], In_Y[6], M, alu_4_p8, S1, S2, out[6], alu_6_p8
  // ALU alu_7: pin names not known; wires that end beside it: In_X[3], In_Y[3], M, alu_5_p8, S1, S2, out[3], alu_2_p4
  // ALU alu_8: pin names not known; wires that end beside it: In_X[7], In_Y[7], M, alu_6_p8, S1, S2, out[7], overflow
endmodule

module _8_Bit_alu_2 (
  input  Carry_In,
  input  [7:0] In_X,
  input  [7:0] In_Y,
  input  [2:0] S1,
  output [7:0] out,
  output overflow___carry_out
);

  wire alu_1_carry_out, alu_2_carry_out, alu_3_carry_out, alu_4_carry_out, alu_5_carry_out, alu_6_carry_out,
       alu_7_carry_out;

  ALU alu_1 (.X(In_X[0]), .Y(In_Y[0]), .out(out[0]), .carry_out(alu_1_carry_out), .carry_in(Carry_In), .M_S1_S2(S1));
  ALU alu_2 (
    .X(In_X[4]), .Y(In_Y[4]), .out(out[4]), .carry_out(alu_2_carry_out), .carry_in(alu_7_carry_out),
    .M_S1_S2(S1));
  ALU alu_3 (
    .X(In_X[1]), .Y(In_Y[1]), .out(out[1]), .carry_out(alu_3_carry_out), .carry_in(alu_1_carry_out),
    .M_S1_S2(S1));
  ALU alu_4 (
    .X(In_X[5]), .Y(In_Y[5]), .out(out[5]), .carry_out(alu_4_carry_out), .carry_in(alu_2_carry_out),
    .M_S1_S2(S1));
  ALU alu_5 (
    .X(In_X[2]), .Y(In_Y[2]), .out(out[2]), .carry_out(alu_5_carry_out), .carry_in(alu_3_carry_out),
    .M_S1_S2(S1));
  ALU alu_6 (
    .X(In_X[6]), .Y(In_Y[6]), .out(out[6]), .carry_out(alu_6_carry_out), .carry_in(alu_4_carry_out),
    .M_S1_S2(S1));
  ALU alu_7 (
    .X(In_X[3]), .Y(In_Y[3]), .out(out[3]), .carry_out(alu_7_carry_out), .carry_in(alu_5_carry_out),
    .M_S1_S2(S1));
  ALU alu_8 (
    .X(In_X[7]), .Y(In_Y[7]), .out(out[7]), .carry_out(overflow___carry_out), .carry_in(alu_6_carry_out),
    .M_S1_S2(S1));
endmodule

module ALU (
  input  carry_in,
  input  X,
  input  Y,
  input  [2:0] M_S1_S2,
  output out,
  output carry_out
);

  wire adder_1_cout, adder_1_out, adder_2_cout, adder_2_out, nand_1_out, nor_1_out, subtractor_1_bout,
       subtractor_1_out, subtractor_2_bout, subtractor_2_out, xor_1_out;

  nor nor_1 (nor_1_out, X, Y);
  nand nand_1 (nand_1_out, X, Y);
  xor xor_1 (xor_1_out, X, Y);
  Adder #(.width(1)) adder_1 (.a(X), .b(Y), .out(adder_1_out), .cin(carry_in), .cout(adder_1_cout));
  Subtractor #(.width(1)) subtractor_1 (.a(X), .b(Y), .out(subtractor_1_out), .bin(carry_in), .bout(subtractor_1_bout));
  Subtractor #(.width(1)) subtractor_2 (
    .a(X), .b(1'b1), .out(subtractor_2_out), .bin(carry_in), .bout(subtractor_2_bout));
  Adder #(.width(1)) adder_2 (.a(X), .b(1'b1), .out(adder_2_out), .cin(carry_in), .cout(adder_2_cout));
  Multiplexer #(.select(3)) multiplexer_1 (
    .in0(nor_1_out), .in1(nand_1_out), .in2(xor_1_out), .in4(adder_1_out), .in5(subtractor_1_out),
    .in6(subtractor_2_out), .in7(adder_2_out), .out(out), .sel(M_S1_S2));  // open: in3, en
  Multiplexer #(.select(3)) multiplexer_2 (
    .in4(adder_1_cout), .in5(subtractor_1_bout), .in6(subtractor_2_bout), .in7(adder_2_cout),
    .out(carry_out), .sel(M_S1_S2));  // open: in0, in1, in2, in3, en
endmodule

module _32_Bit_ALU (
  input  Carry_In,
  input  [31:0] In_X,
  input  [31:0] In_Y,
  input  [2:0] S1,
  output [31:0] out,
  output overflow___carry_out
);

  wire n8_bit_alu_2_1_overflow___carry_out, n8_bit_alu_2_2_overflow___carry_out,
       n8_bit_alu_2_3_overflow___carry_out;

  _8_Bit_alu_2 u_8_bit_alu_2_1 (
    .In_X(In_X[7:0]), .In_Y(In_Y[7:0]), .out(out[7:0]),
    .overflow___carry_out(n8_bit_alu_2_1_overflow___carry_out), .Carry_In(Carry_In), .S1(S1));
  _8_Bit_alu_2 u_8_bit_alu_2_2 (
    .In_X(In_X[15:8]), .In_Y(In_Y[15:8]), .out(out[15:8]),
    .overflow___carry_out(n8_bit_alu_2_2_overflow___carry_out),
    .Carry_In(n8_bit_alu_2_1_overflow___carry_out), .S1(S1));
  _8_Bit_alu_2 u_8_bit_alu_2_3 (
    .In_X(In_X[23:16]), .In_Y(In_Y[23:16]), .out(out[23:16]),
    .overflow___carry_out(n8_bit_alu_2_3_overflow___carry_out),
    .Carry_In(n8_bit_alu_2_2_overflow___carry_out), .S1(S1));
  _8_Bit_alu_2 u_8_bit_alu_2_4 (
    .In_X(In_X[31:24]), .In_Y(In_Y[31:24]), .out(out[31:24]), .overflow___carry_out(overflow___carry_out),
    .Carry_In(n8_bit_alu_2_3_overflow___carry_out), .S1(S1));
endmodule
