// Logisim project flippediyfloppedy.circ as structural Verilog: 1 circuit, main circuit y01d
module y01d (
  input  in_1
);

  wire and_1_out, and_2_out, and_3_out, clock_1_out, clock_2_out, j_k_ff_1_q, j_k_ff_2_q, j_k_ff_3_q,
       j_k_ff_4_q;
  wire [3:0] d_ff_1_q, rom_1_data;

  Clock clock_1 (.out(clock_1_out));
  Clock clock_2 (.out(clock_2_out));
  J_K_Flip_Flop j_k_ff_1 (.J(in_1), .clk(clock_1_out), .K(in_1), .Q(j_k_ff_1_q));  // open: Qn, preset, en, reset
  D_Flip_Flop d_ff_1 (.clk(clock_2_out), .D(rom_1_data[0]), .Q(d_ff_1_q[0]));  // open: Qn, preset, en, reset
  J_K_Flip_Flop j_k_ff_2 (
    .J(j_k_ff_1_q), .clk(clock_1_out), .K(j_k_ff_1_q), .Q(j_k_ff_2_q));  // open: Qn, preset, en, reset
  and and_1 (and_1_out, j_k_ff_1_q, j_k_ff_2_q);
  D_Flip_Flop d_ff_2 (.clk(clock_2_out), .D(rom_1_data[1]), .Q(d_ff_1_q[1]));  // open: Qn, preset, en, reset
  J_K_Flip_Flop j_k_ff_3 (
    .J(and_1_out), .clk(clock_1_out), .K(and_1_out), .Q(j_k_ff_3_q));  // open: Qn, preset, en, reset
  D_Flip_Flop d_ff_3 (.clk(clock_2_out), .D(rom_1_data[2]), .Q(d_ff_1_q[2]));  // open: Qn, preset, en, reset
  and and_2 (and_2_out, and_1_out, j_k_ff_3_q);
  D_Flip_Flop d_ff_4 (.clk(clock_2_out), .D(rom_1_data[3]), .Q(d_ff_1_q[3]));  // open: Qn, preset, en, reset
  J_K_Flip_Flop j_k_ff_4 (
    .J(and_2_out), .clk(clock_1_out), .K(and_2_out), .Q(j_k_ff_4_q));  // open: Qn, preset, en, reset
  and and_3 (and_3_out, and_2_out, j_k_ff_4_q);
  J_K_Flip_Flop j_k_ff_5 (.J(and_3_out), .clk(clock_1_out), .K(and_3_out));  // open: Q, Qn, preset, en, reset
  ROM #(.addrWidth(4), .dataWidth(4)) rom_1 (.addr(d_ff_1_q), .data(rom_1_data));  // open: sel
endmodule
