// Logisim project plusminus.circ as structural Verilog: 1 circuit, main circuit y01d
module y01d (
  input  x,
  input  y,
  input  x_2,
  input  y_2
);

  wire and_1_out, and_2_out, not_1_out, xor_1_out, xor_2_out;

  xor xor_1 (xor_1_out, x, y);
  xor xor_2 (xor_2_out, x_2, y_2);
  not not_1 (not_1_out, x_2);
  and and_1 (and_1_out, x, y);
  and and_2 (and_2_out, not_1_out, y_2);
  // Probe on xor_1_out
  // Probe on and_1_out
  // Probe on xor_2_out
  // Probe on and_2_out
endmodule
